# Fritzing sketch Arduino MEGA 2 moteurs (saved by Fritzing 0.9.3b)

parts:
  Composant1 = Arduino Mega ADK (Rev3)  # not connected
  Mod2 = TMC2209 [package=THT]
  Mod3 = TMC2209 [package=THT]
  M3 = RAMPS_1.4
  M1 = Stepper Motor - Bipolar
  M2 = Stepper Motor - Bipolar
  Power_plug1 = Power plug
  R1 = Resistor [tolerance=±5% resistance=1k package="0402 [SMD]"]
  R2 = Resistor [tolerance=±5% resistance=1k package="0402 [SMD]"]

nets:
  GND: Mod2.PDN2, Mod3.PDN2, M3.GND, M3.Y-1A, M3.E0-MS3, M3.E0-SLP, M3.E1-SLP, M3.D14/Y-MIN, M3.D15/Y-MAX, M3.D18/Z-MIN, M3.D19/Z-MAX, Power_plug1.GND, R1.Pin_0, R1.Pin_1, R2.Pin_0, R2.Pin_1
  N1: M3.E0-2B, M1.D
  N2: M3.E0-2A, M1.C
  N3: M3.E0-1A, M1.A
  N4: M3.E0-1B, M1.B
  N5: M3.E1-2B, M2.D
  N6: M3.E1-2A, M2.C
  N7: M3.E1-1A, M2.A
  N8: M3.E1-1B, M2.B
  +12V: M3.+12V, Power_plug1.VCC

notes:
  Alimentation 12V 5A
  RA
  DC

custom parts:
  TMC2209: TMC2209-LA stepper motor controller and driver. Supply voltage 4.75-28V Iphase up to 1.77A rms (2.5A peak)
  RAMPS_1.4: Ramps 1.4 3d printer driver module. Pcb view has been supressed as not useful. Note you can drag the A4988 stepper controller over the sockets on the card and they will connect correctly (there is currently a Fritzing bug which will say there are connections unrouted however). At present the mega connections are not populated, although with work on schematic that could be done too.
